# Fritzing sketch Breadboard_view_sensor_rumah_kepiting (saved by Fritzing 0.9.3b)
breadboards: 1

parts:
  DS1 = DS18B20 1-Wire Temperature Sensor Probe
  J1 = Screw terminal - 3 pins [package=THT]
  U1 = ESP8266 NodeMCU LoLin base
  R1 = Resistor [tolerance=±5% resistance=4.7k package=THT]
  Squix1 = OLED 0.96" 128x64 I2C SSD1306
  A1 = tds-sensor-meter-v1.0_1

nets:
  GND: DS1.GND, J1.pin1, U1.GND1-0, U1.GND1-1, U1.GND1-2, U1.GND3-2, Squix1.GND, A1.pin3
  N1: DS1.DQ, J1.pin2, U1.D4-0, U1.D4-2, R1.Pin_0
  VDD: DS1.VDD, J1.pin3, U1.3V1-0, U1.3V1-1, U1.3V1-2, U1.3V2-0, U1.3V3-2, R1.Pin_1, Squix1.VCC, A1.pin2
  N2: U1.D1-0, U1.D1-2, Squix1.SCL
  N3: U1.D2-0, U1.D2-2, Squix1.SCA
  N4: U1.A0, A1.pin1

custom parts:
  Screw terminal - 3 pins: Screw terminal with 3 pins (size increased to match part)
  ESP8266 NodeMCU LoLin base: ESP8266 based NodeMCU Base
  : TDS Meter V1.0 Development Board Water Meter Filter Measuring Water Sensor Module.
